# Fritzing sketch diagram (saved by Fritzing 0.9.3b)
breadboards: 1

parts:
  Part1 = Arduino Uno (Rev3) - ICSP
  U1 = RF-LINK_TX [package=rf-link_tx]  # not connected
  R1 = Temperature Sensor (Thermistor) [thermistor_type=NTC package=THT]
  R2 = Resistor [tolerance=±5% resistance=220 package=THT]

nets:
  N1: Part1.A0, R1.pin_1, R2.Pin_1
  N2: Part1.AREF, Part1.5V, R2.Pin_0
  N3: Part1.GND, R1.pin_0
